// Logisim project Muffin Soldiers 4BitALU.circ as structural Verilog
module _4_Bit_ALU (
  input  A3,
  input  A2,
  input  A1,
  input  A0,
  input  B3,
  input  B2,
  input  B1,
  input  B0,
  input  S2,
  input  S1,
  input  S0,
  output OF,
  output R3,
  output R2,
  output R1,
  output R0
);

  wire [3:0] interface_1_r, undriven, undriven_2;

  Hex_Digit_Display hex_digit_display_1 (.value(undriven), .dp(1'b0));
  Hex_Digit_Display hex_digit_display_2 (.value(undriven_2), .dp(1'b0));
  Interface interface_1 (
    .A3(A3), .R3(R3), .A2(A2), .R2(R2), .A1(A1), .R1(R1), .A0(A0), .R0(R0), .B3(B3), .B2(B2), .B1(B1),
    .B0(B0), .S2(S2), .S1(S1), .S0(S0), .R(interface_1_r), .OF(OF));
  Hex_Digit_Display hex_digit_display_3 (.value(interface_1_r), .dp(1'b0));

  // Notes on the sheet:
  //   Kleinprojekt Arithmetic and Logic Unit
  //   Teamname:
  //   ausgeführt von
  //   thomas.wilde@students.fhnw.ch
  //   denis.augsburger@students.fhnw.ch
  //   nicolas.mauchle@students.fhnw.ch
  //   piero.steinger@students.fhnw.ch
  //   Muffin Soldiers
endmodule

module Interface (
  input  A0,
  input  A1,
  input  A2,
  input  A3,
  input  B0,
  input  B1,
  input  B2,
  input  B3,
  input  S0,
  input  S1,
  input  S2,
  output [3:0] R,
  output R0,
  output R1,
  output R2,
  output R3,
  output OF
);

  wire [3:0] S_0_OUT, S_1_OUT, S_2_OUT, S_3_OUT;
  wire [4:0] S_4_OUT, S_5_OUT, S_6_OUT, S_7_OUT;

  OR or_1 (
    .A0(A0), .A1(A1), .A2(A2), .A3(A3), .B0(B0), .B1(B1), .B2(B2), .B3(B3), .R0(S_0_OUT[0]), .R1(S_0_OUT[1]),
    .R2(S_0_OUT[2]), .R3(S_0_OUT[3]));
  AND and_1 (
    .A0(A0), .A1(A1), .A2(A2), .A3(A3), .B0(B0), .B1(B1), .B2(B2), .B3(B3), .R0(S_1_OUT[0]), .R1(S_1_OUT[1]),
    .R2(S_1_OUT[2]), .R3(S_1_OUT[3]));
  \not  not_1 (.A0(A0), .A1(A1), .A2(A2), .A3(A3), .R0(S_2_OUT[0]), .R1(S_2_OUT[1]), .R2(S_2_OUT[2]), .R3(S_2_OUT[3]));
  \not  not_2 (.A0(B0), .A1(B1), .A2(B2), .A3(B3), .R0(S_3_OUT[0]), .R1(S_3_OUT[1]), .R2(S_3_OUT[2]), .R3(S_3_OUT[3]));
  _4Bitaddierer u_4bitaddierer_1 (
    .A0(A0), .A1(A1), .A2(A2), .A3(A3), .B0(B0), .B1(B1), .B2(B2), .B3(B3), .R0(S_4_OUT[0]), .R1(S_4_OUT[1]),
    .R2(S_4_OUT[2]), .R3(S_4_OUT[3]), .C(S_4_OUT[4]));
  times2 times2_1 (
    .A0(A0), .A1(A1), .A2(A2), .A3(A3), .R0(S_6_OUT[0]), .R1(S_6_OUT[1]), .R2(S_6_OUT[2]), .R3(S_6_OUT[3]),
    .C(S_6_OUT[4]));
  times2 times2_2 (
    .A0(A0), .A1(A1), .A2(A2), .A3(A3), .R0(S_7_OUT[0]), .R1(S_7_OUT[1]), .R2(S_7_OUT[2]), .R3(S_7_OUT[3]),
    .C(S_7_OUT[4]));
  Multiplexer #(.select(3), .width(5)) multiplexer_1 (
    .in0({1'b0, S_0_OUT}), .in1({1'b0, S_1_OUT}), .in2({1'b0, S_2_OUT}), .in3({1'b0, S_3_OUT}),
    .in4(S_4_OUT), .in5(S_5_OUT), .in6(S_6_OUT), .in7(S_7_OUT), .out({OF, R}), .sel({S2, S1, S0}), .en(1'b1));

  assign R0 = R[0];
  assign R1 = R[1];
  assign R2 = R[2];
  assign R3 = R[3];

  // Other names for the same wires on the sheet: A_Bits[3:0] = {A3, A2, A1, A0}; B_Bits[3:0] = {B3, B2, B1, B0};
  //   S_Bits[2:0] = {S2, S1, S0}

  // Notes on the sheet:
  //   S = 0 -> A or B
  //   S = 1 -> A and B
  //   S = 2 -> not A
  //   S = 3 -> not B
  //   S = 4 -> A plus B
  //   S = 5 -> A minus B
  //   S = 6 -> A times2
  //   S = 7 -> A times4
endmodule

module Halbadierer (
  input  A,
  input  B,
  output S,
  output C
);

  xor xor_1 (S, A, B);
  and and_1 (C, A, B);
endmodule

module Volladierer (
  input  C,
  input  A,
  input  B,
  output S,
  output C_2
);

  wire Halbaddierer_c, Halbaddierer_s, halbadierer_1_c;

  Halbadierer Halbaddierer (.A(A), .B(B), .S(Halbaddierer_s), .C(Halbaddierer_c));
  Halbadierer halbadierer_1 (.A(C), .B(Halbaddierer_s), .S(S), .C(halbadierer_1_c));
  or or_1 (C_2, halbadierer_1_c, Halbaddierer_c);
endmodule

module _4Bitaddierer (
  input  A0,
  input  A1,
  input  A2,
  input  A3,
  input  B0,
  input  B1,
  input  B2,
  input  B3,
  output R0,
  output R1,
  output R2,
  output R3,
  output C
);

  wire halbadierer_1_c, volladierer_1_c_2, volladierer_2_c_2;

  Halbadierer halbadierer_1 (.A(A0), .B(B0), .S(R0), .C(halbadierer_1_c));
  Volladierer volladierer_1 (.C(halbadierer_1_c), .A(A1), .B(B1), .S(R1), .C_2(volladierer_1_c_2));
  Volladierer volladierer_2 (.C(volladierer_1_c_2), .A(A2), .B(B2), .S(R2), .C_2(volladierer_2_c_2));
  Volladierer volladierer_3 (.C(volladierer_2_c_2), .A(A3), .B(B3), .S(R3), .C_2(C));
endmodule

module times2 (
  input  A0,
  input  A1,
  input  A2,
  input  A3,
  output R0,
  output R1,
  output R2,
  output R3,
  output C
);

  _4Bitaddierer u_4bitaddierer_1 (
    .A0(A0), .A1(A1), .A2(A2), .A3(A3), .B0(A0), .B1(A1), .B2(A2), .B3(A3), .R0(R0), .R1(R1), .R2(R2),
    .R3(R3), .C(C));
endmodule

module times4 (
  input  A0,
  input  A1,
  input  A2,
  input  A3,
  output R0,
  output R1,
  output R2,
  output R3,
  output C
);

  times2 times2_1 (.A0(A0), .A1(A1), .A2(A2), .A3(A3), .R0(R0), .R1(R1), .R2(R2), .R3(R3), .C(C));
endmodule

module AND (
  input  A0,
  input  A1,
  input  A2,
  input  A3,
  input  B0,
  input  B1,
  input  B2,
  input  B3,
  output R0,
  output R1,
  output R2,
  output R3
);

  and and_1 (R0, A0, B0);
  and and_2 (R1, A1, B1);
  and and_3 (R2, A2, B2);
  and and_4 (R3, A3, B3);
endmodule

module OR (
  input  A0,
  input  A1,
  input  A2,
  input  A3,
  input  B0,
  input  B1,
  input  B2,
  input  B3,
  output R0,
  output R1,
  output R2,
  output R3
);

  or or_1 (R0, A0, B0);
  or or_2 (R1, A1, B1);
  or or_3 (R2, A2, B2);
  or or_4 (R3, A3, B3);
endmodule

module \not  (
  input  A0,
  input  A1,
  input  A2,
  input  A3,
  output R0,
  output R1,
  output R2,
  output R3
);

  not not_1 (R0, A0);
  not not_2 (R1, A1);
  not not_3 (R2, A2);
  not not_4 (R3, A3);
endmodule
